# Fritzing sketch connection (saved by Fritzing 0.9.3b)
breadboards: 1

parts:
  부품1 = Arduino Uno (Rev3)
  부품2 = Arduino Mega ADK (Rev3)
  Q1 = NPN-Transistor [package="TO92 [THT]"]
  D1 = Rectifier Diode [part_number=1N4001 package="300 mil [THT]"]
  R1 = Resistor [tolerance=±5% resistance=220 package=THT]
  M1 = DC Motor
  LED1 = Super Flux LED blue [color=Red]
  LED2 = Super Flux LED blue [color=Red]
  LED3 = Super Flux LED blue [color=Red]
  R2 = Resistor [tolerance=±5% resistance=220 package=THT]
  R3 = Resistor [tolerance=±5% resistance=220 package=THT]
  R4 = Resistor [tolerance=±5% resistance=220 package=THT]
  LED4 = Super Flux LED blue [color=Orange]
  LED5 = Super Flux LED blue [color=Orange]
  LED6 = Super Flux LED blue [color=Orange]
  R5 = Resistor [tolerance=±5% resistance=220 package=THT]
  R6 = Resistor [tolerance=±5% resistance=220 package=THT]
  R7 = Resistor [tolerance=±5% resistance=220 package=THT]
  LED7 = Super Flux LED blue [color=Green]
  LED8 = Super Flux LED blue [color=Green]
  LED9 = Super Flux LED blue [color=Green]
  R8 = Resistor [tolerance=±5% resistance=220 package=THT]
  R9 = Resistor [tolerance=±5% resistance=220 package=THT]
  R10 = Resistor [tolerance=±5% resistance=220 package=THT]
  LED10 = Super Flux LED blue [color=Red]
  LED11 = Super Flux LED blue [color=Green]
  R11 = Resistor [tolerance=±5% resistance=220 package=THT]
  R12 = Resistor [tolerance=±5% resistance=220 package=THT]
  S1 = Pushbutton [package="[THT]"]
  J1 = female pin header, 2 pins [form="♀ (female)"]
  J2 = female pin header, 2 pins [form="♀ (female)"]
  J3 = female pin header, 2 pins [form="♀ (female)"]
  J4 = female pin header, 2 pins [form="♀ (female)"]
  J5 = female pin header, 2 pins [form="♀ (female)"]

nets:
  N1: 부품1.D9_PWM, J5.pin2
  N2: 부품1.D4, 부품2.D14/TX3
  N3: 부품1.D5_PWM, 부품2.D15/RX3
  N4: 부품1.5V, J5.pin1
  GND: 부품1.GND, 부품2.GND, Q1.E, LED1.cathode, LED2.cathode, LED3.cathode, LED4.cathode, LED5.cathode, LED6.cathode, LED7.cathode, LED8.cathode, LED9.cathode, LED10.cathode, LED11.cathode, S1.Pin_3, S1.Pin_4, J1.pin1, J4.pin1
  N5: 부품2.D17/RX2, J2.pin1
  N6: 부품2.D16/TX2, J2.pin2, J3.pin1
  N7: 부품2.D12_PWM, R8.Pin_0, R9.Pin_1, R10.Pin_1
  N8: 부품2.D11_PWM, R5.Pin_0, R6.Pin_1, R7.Pin_1
  N9: 부품2.D10_PWM, R2.Pin_0, R3.Pin_1, R4.Pin_1
  N10: 부품2.D9_PWM, R12.Pin_0
  N11: 부품2.D8_PWM, R11.Pin_0
  N12: 부품2.3V3, J1.pin2
  N13: 부품2.D7_PWM, S1.Pin_1, S1.Pin_2
  N14: Q1.B, R1.Pin_1
  N15: Q1.C, D1.anode
  N16: D1.cathode, M1.pin_1
  N17: LED1.anode, R3.Pin_0
  N18: LED2.anode, R2.Pin_1
  N19: LED3.anode, R4.Pin_0
  N20: LED4.anode, R6.Pin_0
  N21: LED5.anode, R5.Pin_1
  N22: LED6.anode, R7.Pin_0
  N23: LED7.anode, R9.Pin_0
  N24: LED8.anode, R8.Pin_1
  N25: LED9.anode, R10.Pin_0
  N26: LED10.anode, R11.Pin_1
  N27: LED11.anode, R12.Pin_1

notes:
  T R 5 G 3
  X X V N .3
  D V
  [NFC]
  G V I
  N C N
  D C
  [스피커
  모듈]
