# Fritzing sketch connection_with_yellow_block (saved by Fritzing 0.9.3b)

parts:
  부품1 = Arduino Mega ADK (Rev3)
  부품2 = Arduino Uno (Rev3)
  LED2 = LED - 5mm [color="Red (633nm)" package="5 mm [THT]"]
  LED3 = LED - 5mm [color="Orange (620nm)" package="5 mm [THT]"]
  LED4 = LED - 5mm [color="Green (555nm)" package="5 mm [THT]"]
  LED6 = LED - 5mm [color="Red (633nm)" package="5 mm [THT]"]
  LED7 = LED - 5mm [color="Green (555nm)" package="5 mm [THT]"]
  RHT1 = Humidity and Temperature Sensor RHT03
  M1 = DC Motor
  Q1 = PNP-Transistor [package="TO92 [THT]"]
  LED8 = DUO LED RG [package="5 mm [THT]"]
  LED9 = LED - 5mm [color="Yellow (585nm)" package="5 mm [THT]"]

nets:
  N1: 부품1.D19/RX1, RHT1.Vcc
  N2: 부품1.D18/TX1, RHT1.Data-signal
  N3: 부품1.D15/RX3, 부품2.D5_PWM
  N4: 부품1.D14/TX3, 부품2.D4
  GND: 부품1.GND, 부품2.GND, RHT1.GND_2, Q1.E
  N5: 부품1.D12_PWM, LED4.anode
  N6: 부품1.D11_PWM, LED3.anode
  N7: 부품1.D10_PWM, LED2.anode
  N8: 부품1.D9_PWM, LED7.anode
  N9: 부품1.D8_PWM, LED6.anode
  N10: 부품1.5V, RHT1.GND_1
  N11: 부품1.D6_PWM, LED8.green_anode
  N12: 부품1.D40, LED9.anode
  N13: 부품2.D9_PWM, Q1.C
  N14: 부품2.D10_PWM/SS, M1.pin_1
  N15: 부품2.5V, Q1.B
  N16: LED2.cathode, LED4.cathode
  N17: LED6.cathode, LED7.cathode

notes:
  NFC MODULE
  SOUND AMP MODULE
  TX
  RX
  5V
  GND
  GND
  VCC
  IN
  NEO PIXEL RING
  GND
  VCC
  DIN
